# Fritzing sketch raspi_poti_ads1115 (saved by Fritzing 0.9.4)

parts:
  Raspberry_Pi1 = Raspberry Pi 2
  Part1 = Adafruit ADS1115 16Bit I2C ADC [part_number="Adafruit #1085"]
  U1 = POT [package=pot_mammoth]

nets:
  3V3: Raspberry_Pi1.3v3, Raspberry_Pi1.3V3, Part1.VDD, U1.E
  N1: Raspberry_Pi1.GPIO2, Part1.SDA
  N2: Raspberry_Pi1.GPIO3, Part1.SCL
  GND: Raspberry_Pi1.GND, Part1.GND, U1.S
  N3: Part1.AIN0, U1.A

custom parts:
  Adafruit ADS1115 16Bit I2C ADC: For microcontrollers without an analog-to-digital converter or when you want a higher-precision ADC, the ADS1115 provides 16-bit precision at 860 samples/second over I2C. The chip can be configured as 4 single-ended input channels, or two differential channels. As a nice bonus, it even includes a programmable gain amplifier, up to x16, to help boost up smaller single/differential signals to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
